// Digital circuit Controler.dig as structural Verilog
module Controler (
);

  wire demultiplexer_1_out_4, demultiplexer_1_out_5, demultiplexer_1_out_6, demultiplexer_1_out_7,
       register_8_bits_parallel_1_p1, register_8_bits_parallel_1_p2, register_8_bits_parallel_2_p2,
       register_8_bits_parallel_3_p2, register_8_bits_parallel_4_p2;

  // Register_8_bits_Parallel register_8_bits_parallel_1: pin names not known; wires that end beside it: register_8_bits_parallel_1_p1, register_8_bits_parallel_1_p2, register_8_bits_parallel_1_p2, 1'b0
  // Register_8_bits_Parallel register_8_bits_parallel_2: pin names not known; wires that end beside it: register_8_bits_parallel_1_p1, register_8_bits_parallel_2_p2, register_8_bits_parallel_2_p2, 1'b0
  // Register_8_bits_Parallel register_8_bits_parallel_3: pin names not known; wires that end beside it: register_8_bits_parallel_1_p1, register_8_bits_parallel_3_p2, register_8_bits_parallel_3_p2, 1'b0
  // Register_8_bits_Parallel register_8_bits_parallel_4: pin names not known; wires that end beside it: register_8_bits_parallel_1_p1, register_8_bits_parallel_4_p2, register_8_bits_parallel_4_p2, 1'b0
  Demultiplexer #(.Selector_Bits(3)) demultiplexer_1 (
    .in(1'b1), .out_0(register_8_bits_parallel_1_p2), .out_1(register_8_bits_parallel_2_p2),
    .out_2(register_8_bits_parallel_3_p2), .out_3(register_8_bits_parallel_4_p2),
    .out_4(demultiplexer_1_out_4), .out_5(demultiplexer_1_out_5), .out_6(demultiplexer_1_out_6),
    .out_7(demultiplexer_1_out_7));  // open: sel
  // Register_8_bits_Parallel register_8_bits_parallel_5: pin names not known; wires that end beside it: register_8_bits_parallel_1_p1, demultiplexer_1_out_4, demultiplexer_1_out_4, 1'b0
  // Register_8_bits_Parallel register_8_bits_parallel_6: pin names not known; wires that end beside it: register_8_bits_parallel_1_p1, demultiplexer_1_out_5, demultiplexer_1_out_5, 1'b0
  // Register_8_bits_Parallel register_8_bits_parallel_7: pin names not known; wires that end beside it: register_8_bits_parallel_1_p1, demultiplexer_1_out_6, demultiplexer_1_out_6, 1'b0
  // Register_8_bits_Parallel register_8_bits_parallel_8: pin names not known; wires that end beside it: register_8_bits_parallel_1_p1, demultiplexer_1_out_7, demultiplexer_1_out_7, 1'b0
endmodule
