// Digital circuit Divisor.dig as structural Verilog
module Divisor (
);

  wire and_1_out, and_2_out, and_3_out, and_4_out, and_5_out, and_6_out, or_1_out, or_2_out, or_3_out,
       undriven, undriven_2, undriven_3, undriven_4, undriven_5, undriven_6, xor_1_out, xor_2_out, xor_3_out,
       xor_4_out, xor_5_out, xor_6_out;

  and and_1 (and_1_out, undriven_2, undriven);
  and and_2 (and_2_out, xor_1_out, or_2_out);
  or or_1 (or_1_out, and_1_out, and_2_out);
  xor xor_1 (xor_1_out, undriven, undriven_2);
  xor xor_2 (xor_2_out, or_2_out, xor_1_out);
  and and_3 (and_3_out, undriven_4, undriven_3);
  xor xor_3 (xor_3_out, undriven_3, undriven_4);
  and and_4 (and_4_out, xor_3_out, or_3_out);
  or or_2 (or_2_out, and_3_out, and_4_out);
  and and_5 (and_5_out, undriven_6, undriven_5);
  xor xor_4 (xor_4_out, or_3_out, xor_3_out);
  and and_6 (and_6_out, xor_5_out, 1'b1);
  or or_3 (or_3_out, and_5_out, and_6_out);
  xor xor_5 (xor_5_out, undriven_5, undriven_6);
  xor xor_6 (xor_6_out, 1'b1, xor_5_out);
endmodule
