// Digital circuit Memory Loader.dig as structural Verilog
module Memory_Loader (
  input  C,
  input  CE,
  input  SE,
  output [19:0] S
);

  wire [7:0] counter_1_out, eepromdualport_1_d;
  wire [9:9] and_1_out;

  and and_1 (and_1_out[9], C, CE);
  Counter #(.Bits(8)) counter_1 (.en(1'b1), .C(and_1_out[9]), .clr(1'b0), .out(counter_1_out));  // open: ovf
  LED led_1 (.in(eepromdualport_1_d[7]));
  LED led_2 (.in(eepromdualport_1_d[6]));
  LED led_3 (.in(eepromdualport_1_d[5]));
  LED led_4 (.in(eepromdualport_1_d[4]));
  LED led_5 (.in(eepromdualport_1_d[3]));
  EEPROMDualPort #(.AddrBits(8), .Bits(8)) eepromdualport_1 (
    .A(counter_1_out), .Din({8{1'b1}}), .str(1'b0), .C(1'b0), .ld(1'b1), .D(eepromdualport_1_d));
  LED led_6 (.in(eepromdualport_1_d[2]));
  LED led_7 (.in(eepromdualport_1_d[1]));
  LED led_8 (.in(eepromdualport_1_d[0]));
  assign S = SE ? {eepromdualport_1_d, 2'b00, and_1_out[9], CE, counter_1_out} : 20'bz;  // Driver driver_1

  // Notes on the sheet:
  //   C: Hz: 50
  //   contents of eepromdualport_1 (hex, n*v repeats v):
  //   a98670,f69b5,0,98bd91,a7dd0c,a98ac7,9009,a7dd0c,9009,9009,9009
  //   ,a98ac7,9009,9009,a7dd0c,a7dd0c,a7dd0c,9009,a98ac7,9009,f69b5
  //   ,a7dd0c,9009,0,a98670,f69b5,0,98bd91,9009,0,98bd91,9009,9009,f69b5
  //   ,a7dd0c,40249,f69b5,0,98bd91,40249,a7dd0c,40249,9009,f69b5,a7dd0c,a7dd0c
  //   ,40249,a98ac7,a98ac7,a98ac7,0,9009,0,98bd91,40249,9009,a98670
  //   ,f69b5,0,98bd91,40249,a98ac7,40249,9009,40249,a98ac7,a98ac7,f69b5
  //   ,a98670,f69b5,0,98bd91,0,a7dd0c,a98ac7,0,a98670,f69b5,0,98bd91
  //   ,a98ac7,0,9009,f69b5,a98ac7,9009,f69b5,a98ac7,9009,a98ac7,0,a7dd0c
  //   ,9009,f69b5,a7dd0c,a98ac7,f69b5,a98ac7,0,98bd91,a98ac7,a98ac7
  //   ,0,a98ac7,0,a98ac7,9009,a98ac7,9009,a7dd0c,a98ac7,9009,a98670
  //   ,f69b5,0,98bd91,a7dd0c,a98ac7,9009,a7dd0c,9009,9009,9009,a98ac7
  //   ,9009,9009,a7dd0c,a7dd0c,a7dd0c,9009,a98ac7,9009,f69b5,a7dd0c
  //   ,9009,0,a98670,f69b5,0,98bd91,9009,0,98bd91,9009,9009,f69b5,a7dd0c
  //   ,40249,f69b5,0,98bd91,40249,a7dd0c,40249,9009,f69b5,a7dd0c,a7dd0c
  //   ,40249,a98ac7,a98ac7,a98ac7,0,9009,0,98bd91,40249,9009,a98670
  //   ,f69b5,0,98bd91,40249,a98ac7,40249,9009,40249,a98ac7,a98ac7,f69b5
  //   ,a98670,f69b5,0,98bd91,0,a7dd0c,a98ac7,0,a98670,f69b5,0,98bd91
  //   ,a98ac7,0,9009,f69b5,a98ac7,9009,f69b5,a98ac7,9009,a98ac7,0,a7dd0c
  //   ,9009,f69b5,a7dd0c,a98ac7,f69b5,a98ac7,0,98bd91,a98ac7,a98ac7
  //   ,0,a98ac7,0,a98ac7,9009,a98ac7,9009,a7dd0c,a98ac7,9009,a98670
  //   ,f69b5,0,98bd91,a7dd0c,a98ac7,9009,a7dd0c,9009,9009,9009,a98ac7
  //   ,9009,9009,a7dd0c,a7dd0c,a7dd0c,9009,a98ac7,9009,f69b5,a7dd0c
  //   ,9009,0,a98670,f69b5,0,98bd91,9009,0,98bd91,9009
endmodule
